# Fritzing sketch ambient_light (saved by Fritzing 0.9.2b)
breadboards: 1

parts:
  R1 = Photocell (LDR) [package=THT]
  R2 = Resistor [tolerance=±5% resistance=10k package=THT]

nets:
  N1: R1.pin_1, R2.Pin_0

notes:
  Layout from
  https://mbientlab.com/docs/
  MetaWearCPSv0.5.pdf (2016-03-08)
